# Fritzing sketch photoresistors (saved by Fritzing 0.9.7b)
breadboards: 1

parts:
  Part1 = Arduino Mega ADK (Rev3)
  R1 = PHOTOCELL [package=photocell]  # not connected
  R2 = Resistor [tolerance=±5% resistance=220 package="2010 [SMD]"]
  R3 = PHOTOCELL [package=photocell]  # not connected
  R4 = Resistor [tolerance=±5% resistance=220 package="2010 [SMD]"]
  R5 = PHOTOCELL [package=photocell]  # not connected
  R6 = Resistor [tolerance=±5% resistance=220 package="2010 [SMD]"]
  R7 = PHOTOCELL [package=photocell]
  R8 = Resistor [tolerance=±5% resistance=220 package="2010 [SMD]"]
  R9 = PHOTOCELL [package=photocell]  # not connected
  R10 = Resistor [tolerance=±5% resistance=220 package="2010 [SMD]"]
  R11 = PHOTOCELL [package=photocell]  # not connected
  R12 = Resistor [tolerance=±5% resistance=220 package="2010 [SMD]"]
  R13 = PHOTOCELL [package=photocell]  # not connected
  R14 = Resistor [tolerance=±5% resistance=220 package="2010 [SMD]"]

nets:
  N1: Part1.A8, R2.Pin_1
  N2: Part1.A9, R4.Pin_1
  N3: Part1.A10, R6.Pin_1
  N4: Part1.A11, R7.P$1, R8.Pin_1
  N5: Part1.A12, R10.Pin_1
  N6: Part1.A13, R12.Pin_1
  N7: Part1.A14, R14.Pin_1
  N8: Part1.5V, R2.Pin_0, R4.Pin_0, R6.Pin_0, R8.Pin_0, R10.Pin_0, R12.Pin_0, R14.Pin_0
  N9: Part1.GND, R7.P$2
