# Fritzing sketch potentiometer (saved by Fritzing 0.9.7b)
breadboards: 1

parts:
  Part1 = Arduino Mega ADK (Rev3)
  R4 = TRIMPOT [package=3362u-2]
  R3 = TRIMPOT [package=3362u-2]
  R2 = TRIMPOT [package=3362u-2]
  R1 = TRIMPOT [package=3362u-2]

nets:
  N1: Part1.A0, R1.WIPER
  N2: Part1.A1, R2.WIPER
  N3: Part1.A2, R3.WIPER
  N4: Part1.A3, R4.WIPER
  N5: Part1.GND, R4.CW, R3.CW, R2.CW, R1.CW
  N6: Part1.5V, R4.CCW, R3.CCW, R2.CCW, R1.CCW

notes:
  Speed
  P
  I
  D
